# Fritzing sketch ArduinoBusyBoard (saved by Fritzing 0.9.3b)
circuit board: 8.46667cm x 5.64444cm
stripboards: 2
breadboards: 1

parts:
  Part1 = Arduino Mega 2560 (Rev3)
  J1 = female pin header, 2 pins [form="♀ (female)"]
  J2 = female pin header, 2 pins [form="♀ (female)"]
  U1 = 74HC595 [package="DIP16 [THT]"]
  U2 = 74HC595 [package="DIP16 [THT]"]
  R1 = Resistor [tolerance=±5% resistance=330 package=THT]
  R2 = Resistor [tolerance=±5% resistance=330 package=THT]
  R3 = Resistor [tolerance=±5% resistance=330 package=THT]
  R4 = Resistor [tolerance=±5% resistance=330 package=THT]
  R5 = Resistor [tolerance=±5% resistance=330 package=THT]
  R6 = Resistor [tolerance=±5% resistance=330 package=THT]
  R7 = Resistor [tolerance=±5% resistance=330 package=THT]
  R8 = Resistor [tolerance=±5% resistance=330 package=THT]
  R9 = Resistor [tolerance=±5% resistance=330 package=THT]
  R10 = Resistor [tolerance=±5% resistance=330 package=THT]
  R11 = Resistor [tolerance=±5% resistance=330 package=THT]
  R12 = Resistor [tolerance=±5% resistance=330 package=THT]
  R13 = Resistor [tolerance=±5% resistance=330 package=THT]
  R14 = Resistor [tolerance=±5% resistance=330 package=THT]
  R15 = Resistor [tolerance=±5% resistance=330 package=THT]
  R16 = Resistor [tolerance=±5% resistance=330 package=THT]
  J3 = female pin header, 7 pins [form="♀ (female)"]
  J4 = female pin header, 7 pins [form="♀ (female)"]
  C1 = Ceramic Capacitor [capacitance=100nF package="100 mil [THT, multilayer]"]
  C2 = Ceramic Capacitor [capacitance=100nF package="100 mil [THT, multilayer]"]
  J5 = female pin header, 2 pins [form="♀ (female)"]
  J6 = female pin header, 1 pin [form="♀ (female)"]
  J7 = female pin header, 2 pins [form="♀ (female)"]
  R17 = Resistor [tolerance=±5% resistance=330 package=THT]
  J8 = female pin header, 1 pin [form="♀ (female)"]
  DFRobot_DFPlayer_Mini2 = DFRobot DFPlayer Mini [part_number=DFR0299]
  R18 = Resistor [tolerance=±5% resistance=10k package=THT]
  R19 = Resistor [tolerance=±5% resistance=10k package=THT]
  R20 = Resistor [tolerance=±1% resistance=10k package=THT]
  R21 = Resistor [tolerance=±5% resistance=10k package=THT]
  J10 = female pin header, 2 pins [form="♀ (female)"]
  J11 = female pin header, 2 pins [form="♀ (female)"]
  J12 = female pin header, 2 pins [form="♀ (female)"]
  J13 = female pin header, 2 pins [form="♀ (female)"]
  R22 = Resistor [tolerance=±5% resistance=330 package=THT]
  R23 = Resistor [tolerance=±5% resistance=330 package=THT]
  R24 = Resistor [tolerance=±5% resistance=330 package=THT]
  R25 = Resistor [tolerance=±5% resistance=10k package=THT]
  R26 = Resistor [tolerance=±5% resistance=470 package=THT]
  J16 = female pin header, 1 pin [form="♀ (female)"]
  J17 = female pin header, 1 pin [form="♀ (female)"]
  J18 = female pin header, 2 pins [form="♀ (female)"]
  R27 = Resistor [tolerance=±5% resistance=1k package=THT]
  J19 = female pin header, 2 pins [form="♀ (female)"]
  J20 = female pin header, 2 pins [form="♀ (female)"]
  R28 = Resistor [tolerance=±5% resistance=330 package=THT]
  R29 = Resistor [tolerance=±5% resistance=330 package=THT]
  J15 = female pin header, 5 pins [form="♀ (female)"]
  J21 = female pin header, 1 pin [form="♀ (female)"]
  J22 = female pin header, 10 pins [form="♀ (female)"]
  J23 = female pin header, 10 pins [form="♀ (female)"]
  J24 = female pin header, 10 pins [form="♀ (female)"]
  J25 = female pin header, 10 pins [form="♀ (female)"]
  J26 = female pin header, 3 pins [form="♀ (female)"]
  J27 = female pin header, 3 pins [form="♀ (female)"]
  LED1 = LED - 5mm [color="Yellow (595nm)" package="5 mm [THT]"]
  LED2 = LED - 5mm [color="Yellow (595nm)" package="5 mm [THT]"]
  LED3 = LED - 5mm [color="Yellow (595nm)" package="5 mm [THT]"]
  LED4 = LED - 5mm [color="Yellow (595nm)" package="5 mm [THT]"]
  LED5 = LED - 5mm [color="Yellow (595nm)" package="5 mm [THT]"]
  LED6 = LED - 5mm [color="Yellow (595nm)" package="5 mm [THT]"]
  LED7 = LED - 5mm [color="Yellow (595nm)" package="5 mm [THT]"]
  LED8 = LED - 5mm [color="Yellow (595nm)" package="5 mm [THT]"]
  LED9 = LED - 5mm [color="Yellow (595nm)" package="5 mm [THT]"]
  LED10 = LED - 5mm [color="Yellow (595nm)" package="5 mm [THT]"]
  LED11 = LED - 5mm [color="Red (660nm)" package="5 mm [THT]"]
  LED12 = LED - 5mm [color="Blue (525nm)" package="5 mm [THT]"]
  LED13 = LED - 5mm [color="Green (570nm)" package="5 mm [THT]"]
  LED14 = LED - 5mm [color="Yellow (595nm)" package="5 mm [THT]"]
  LED15 = LED - 5mm [color="Red (660nm)" package="5 mm [THT]"]
  LED16 = LED - 5mm [color="Blue (525nm)" package="5 mm [THT]"]
  LED17 = LED - 5mm [color="Green (570nm)" package="5 mm [THT]"]
  SP1 = SPEAKER [package=pcb_mount_speaker]
  J28 = female pin header, 5 pins [form="♀ (female)"]
  J29 = female pin header, 5 pins [form="♀ (female)"]
  J30 = female pin header, 5 pins [form="♀ (female)"]
  LED18 = RGB LED (com. cathode, rbg) [package="5 mm [THT]"]
  R30 = Photocell (LDR) [package=THT]
  BUTTON1 = Waterproof Pushbutton (red)
  BUTTON2 = Waterproof Pushbutton (white)
  BUTTON3 = Waterproof Pushbutton (blue)
  BUTTON4 = Waterproof Pushbutton (green)
  S1 = Toggle Switch [package=THT]
  S2 = Toggle Switch [package=THT]
  S3 = Toggle Switch [package=THT]
  J31 = Basic Force Sensing Resistor (FSR) [package=THT]
  Part2 = MPR121 Breakout
  R31 = Rotary Potentiometer (Large) [maximum_resistance=100kΩ package=THT]
  R32 = Rotary Potentiometer (Large) [maximum_resistance=100kΩ package=THT]
  R33 = Rotary Potentiometer (Large) [maximum_resistance=100kΩ package=THT]
  J32 = Infrared Proximity Sensor
  Voltmeter1 = Voltmeter
  U3 = SLIDER [package=slider]
  ENCODER1 = Rotary Encoder with Knob
  Part3 = Adafruit TB6612 DC and Stepper Motor Driver [part_number="Adafruit #2448"]
  M1 = RioRand LM2596
  M2 = RioRand LM2596
  Power_plug1 = Power plug
  U4 = WS2812 RGB LED strip
  U5 = Vibration Motor- ROB-08449 [package=vibe-motor-10mm]
  F1 = Fan - Ventilador [package=THT]
  J14 = female pin header, 4 pins [form="♀ (female)"]
  R34 = Trimmer Potentiometer [maximum_resistance=10kΩ package=THT]

nets:
  N1: Part1.A8, R21.Pin_0, J12.pin1, J13.pin1, J31.pin_0
  N2: Part1.A9, R34.wiper
  N3: Part1.A0, R31.leg2
  N4: Part1.A1, R32.leg2
  N5: Part1.A2, R33.leg2
  N6: Part1.A3, J32.Vout
  N7: Part1.A4, ENCODER1.no_name_yet#3
  N8: Part1.A5, ENCODER1.no_name_yet#1
  N9: Part1.A6, ENCODER1.no_name_yet#4
  N10: Part1.A7, U3.A
  N11: Part1.D21/SCL, Part2.SCL
  N12: Part1.D20/SDA, Part2.SDA
  N13: Part1.D11_PWM, R27.Pin_1, J19.pin1
  N14: Part1.D10_PWM, DFRobot_DFPlayer_Mini2.TX, J19.pin2
  N15: Part1.D9_PWM, R23.Pin_1, J14.pin2
  N16: Part1.D8_PWM, R22.Pin_1, J14.pin3
  VCC: Part1.5V, J1.pin2, J2.pin2, U1.MR, U1.VCC, U2.MR, U2.VCC, C1.1, C2.1, DFRobot_DFPlayer_Mini2.VCC, R25.Pin_0, J18.pin2, R28.Pin_1, R29.Pin_1, J28.pin1, J28.pin2, J28.pin3, J28.pin4, J28.pin5, J29.pin1, J29.pin2, J29.pin3, J29.pin4, J29.pin5, J30.pin1, J30.pin2, J30.pin3, J30.pin4, J30.pin5, BUTTON3.no_name_yet#4, BUTTON4.no_name_yet#4, S1.L1, S2.L1, S3.L1, J31.pin_1, Part2.3.3V, R31.leg1, R32.leg1, R33.leg1, J32.Vcc, U3.S, Part3.VCC, R34.leg1
  GND: Part1.GND, J1.pin1, J2.pin1, U1.GND, U1.OE, U2.GND, U2.OE, C1.0, C2.0, DFRobot_DFPlayer_Mini2.GND-1, DFRobot_DFPlayer_Mini2.GND-2, R18.Pin_0, R19.Pin_1, R20.Pin_0, R21.Pin_1, J18.pin1, J21.pin1, J22.pin1, J22.pin2, J22.pin3, J22.pin4, J22.pin5, J22.pin6, J22.pin7, J22.pin8, J22.pin9, J22.pin10, J23.pin1, J23.pin2, J23.pin3, J23.pin4, J23.pin5, J23.pin6, J23.pin7, J23.pin8, J23.pin9, J23.pin10, J24.pin1, J24.pin2, J24.pin3, J24.pin4, J24.pin5, J24.pin6, J24.pin7, J24.pin8, J24.pin9, J24.pin10, J25.pin1, J25.pin2, J25.pin3, J25.pin4, J25.pin5, J25.pin6, J25.pin7, J25.pin8, J25.pin9, J25.pin10, J26.pin1, J26.pin2, J26.pin3, J27.pin1, J27.pin2, J27.pin3, LED1.cathode, LED2.cathode, LED3.cathode, LED4.cathode, LED5.cathode, LED6.cathode, LED7.cathode, LED8.cathode, LED9.cathode, LED10.cathode, LED11.cathode, LED12.cathode, LED13.cathode, LED14.cathode, LED15.cathode, LED16.cathode, LED17.cathode, LED18.common_cathode, R30.pin_0, BUTTON1.no_name_yet#1, BUTTON1.no_name_yet#5, BUTTON2.no_name_yet#1, BUTTON2.no_name_yet#5, BUTTON3.no_name_yet#1, BUTTON3.no_name_yet#5, BUTTON4.no_name_yet#1, BUTTON4.no_name_yet#2, BUTTON4.no_name_yet#5, S1.COM, S2.COM, S3.COM, Part2.GND, R31.wiper, R32.wiper, R33.wiper, J32.GND, Voltmeter1.Com, U3.E, ENCODER1.no_name_yet#2, ENCODER1.no_name_yet#5, Part3.GND, M1.Pin_4, M2.Pin_4, U4.GND, R34.leg2
  N17: Part1.D2_PWM, Part3.PWMA
  N18: Part1.D3_PWM, Part3.PWMB
  N19: Part1.D4_PWM, Voltmeter1.Positive
  N20: Part1.D6_PWM, U4.DIN
  N21: Part1.D7_PWM, R24.Pin_1, J14.pin1
  N22: Part1.D22, U1.DS, J5.pin1
  N23: Part1.D23, U1.SH_CP, U2.SH_CP, J7.pin1
  N24: Part1.D24, U1.ST_CP, U2.ST_CP, J7.pin2
  N25: Part1.D25, R17.Pin_1, J8.pin1
  N26: Part1.D26, BUTTON1.no_name_yet#2, BUTTON1.no_name_yet#3
  N27: Part1.D27, R18.Pin_1, J10.pin2, J11.pin2, S1.L2
  N28: Part1.D28, BUTTON3.no_name_yet#3
  N29: Part1.D29, R19.Pin_0, J10.pin1, J11.pin1, S2.L2
  N30: Part1.D30, BUTTON4.no_name_yet#3
  N31: Part1.D31, R20.Pin_1, J12.pin2, J13.pin2, S3.L2
  N32: Part1.D32, BUTTON2.no_name_yet#3
  N33: Part1.D33, R26.Pin_1, J17.pin1
  N34: Part1.D42, Part3.BIN2
  N35: Part1.D43, Part3.BIN1
  N36: Part1.D44, Part3.AIN2
  N37: Part1.D45, Part3.AIN1
  N38: Part1.D52, Part3.STBY
  N39: U1.Q1, R2.Pin_1
  N40: U1.Q2, R3.Pin_1
  N41: U1.Q3, R4.Pin_1
  N42: U1.Q4, R5.Pin_1
  N43: U1.Q5, R6.Pin_1
  N44: U1.Q6, R7.Pin_1
  N45: U1.Q7, R8.Pin_1
  N46: U1.Q7', U2.Q7', U2.DS
  N47: U1.Q0, R1.Pin_0
  N48: U2.Q1, R10.Pin_1
  N49: U2.Q2, R11.Pin_1
  N50: U2.Q3, R12.Pin_1
  N51: U2.Q4, R13.Pin_1
  N52: U2.Q5, R14.Pin_1
  N53: U2.Q6, R15.Pin_1
  N54: U2.Q7, R16.Pin_1
  N55: U2.Q0, R9.Pin_0
  N56: R1.Pin_1, J5.pin2, LED1.anode
  N57: R2.Pin_0, J3.pin7, LED2.anode
  N58: R3.Pin_0, J3.pin6, LED3.anode
  N59: R4.Pin_0, J3.pin5, LED4.anode
  N60: R5.Pin_0, J3.pin4, LED5.anode
  N61: R6.Pin_0, J3.pin3, LED6.anode
  N62: R7.Pin_0, J3.pin2, LED7.anode
  N63: R8.Pin_0, J3.pin1, LED8.anode
  N64: R9.Pin_1, J6.pin1, LED9.anode
  N65: R10.Pin_0, J4.pin7, LED10.anode
  N66: R11.Pin_0, J4.pin6, LED13.anode
  N67: R12.Pin_0, J4.pin5, LED12.anode
  N68: R13.Pin_0, J4.pin4, LED11.anode
  N69: R14.Pin_0, J4.pin3, LED14.anode
  N70: R15.Pin_0, J4.pin2, LED15.anode
  N71: R16.Pin_0, J4.pin1, LED16.anode
  N72: R17.Pin_0, LED17.anode, J14.pin4
  N73: DFRobot_DFPlayer_Mini2.RX, R27.Pin_0
  N74: DFRobot_DFPlayer_Mini2.SPK_1, J20.pin2, SP1.-
  N75: DFRobot_DFPlayer_Mini2.SPK_2, J20.pin1, SP1.+
  N76: R22.Pin_0, J15.pin5, LED18.green_anode
  N77: R23.Pin_0, J15.pin4, LED18.blue_anode
  N78: R24.Pin_0, J15.pin3, LED18.red_anode
  N79: R25.Pin_1, R26.Pin_0, J16.pin1, R30.pin_1
  N80: R28.Pin_0, J15.pin2, BUTTON1.no_name_yet#4
  N81: R29.Pin_0, J15.pin1, BUTTON2.no_name_yet#4
  N82: Part3.PWRIN, M1.Pin_3
  N83: Part3.MOTORA1, F1.5V
  N84: Part3.MOTORA2, F1.GND
  N85: Part3.MOTORB2, U5.+
  N86: Part3.MOTORB1, U5.-
  N87: M1.Pin_1, M2.Pin_1, Power_plug1.VCC
  N88: M1.Pin_2, M2.Pin_2, Power_plug1.GND
  N89: M2.Pin_3, U4.VCC

notes:
  Phone
  Arduino
  Phone Y=GND
  Plastic Button / Red
  Plastic Button / Yellow
  Yellow Toggle
  White Toggle
  Red Toggle
  Duck
  RGB Red
  RGB Green
  RGB Blue
  Neopixels V1
  Motors V2
  Hinge

custom parts:
  Waterproof Pushbutton (red): Waterproof Illuminated Pushbutton (red)
  Waterproof Pushbutton (white): Waterproof Illuminated Pushbutton (white)
  Waterproof Pushbutton (blue): Waterproof Illuminated Pushbutton (blue)
  Waterproof Pushbutton (green): Waterproof Illuminated Pushbutton (green)
  Voltmeter: A Standard Multimeter in Current mode
  Rotary Encoder with Knob: Rotary Encoder with 1/4" Shaft and Knob
  Adafruit TB6612 DC and Stepper Motor Driver: Spin two DC motors, step one bi-polar or uni-polar stepper, or fire off two solenoids with 1.2A per channel using the TB6612. These are perhaps better known as "the drivers in our assembled Adafruit Motorshield or Motor HAT." We really like these dual H-bridges, so if you want to control motors without a shield or HAT these are easy to include on any solderless breadboard or perma-proto.
  WS2812 RGB LED strip: WS2812 strip
  Fan - Ventilador: Ventilador de 2 pines, se encuentra comunmente en computadoras de escritorio
