# Fritzing sketch ArduinoBusyBoardOLD (saved by Fritzing 0.9.3b)
breadboards: 2
stripboards: 1

parts:
  Part1 = Arduino Mega 2560 (Rev3)
  SR1 = 74HC595 [package="DIP16 [THT]"]
  SR2 = 74HC595 [package="DIP16 [THT]"]
  C1 = Ceramic Capacitor [capacitance=100nF package="200 mil [THT, multilayer]"]
  C1_2 = Ceramic Capacitor [capacitance=100nF package="200 mil [THT, multilayer]"]
  C1_3 = Ceramic Capacitor [capacitance=100nF voltage=6.3V package="100 mil [THT, multilayer]"]
  PHLED0 = LED - 5mm [color="Yellow (595nm)" package="5 mm [THT]"]
  C2 = Ceramic Capacitor [capacitance=100nF package="100 mil [THT, multilayer]"]
  R1 = Resistor Mini [tolerance=±5% resistance=470 package=THT]
  PHLED1 = LED - 5mm [color="Yellow (595nm)" package="5 mm [THT]"]
  PHLED2 = LED - 5mm [color="Yellow (595nm)" package="5 mm [THT]"]
  PHLED3 = LED - 5mm [color="Yellow (595nm)" package="5 mm [THT]"]
  PHLED4 = LED - 5mm [color="Yellow (595nm)" package="5 mm [THT]"]
  PHLED5 = LED - 5mm [color="Yellow (595nm)" package="5 mm [THT]"]
  PHLED6 = LED - 5mm [color="Yellow (595nm)" package="5 mm [THT]"]
  PHLED7 = LED - 5mm [color="Yellow (595nm)" package="5 mm [THT]"]
  PHLED8 = LED - 5mm [color="Yellow (595nm)" package="5 mm [THT]"]
  PHLED9 = LED - 5mm [color="Yellow (595nm)" package="5 mm [THT]"]
  R2 = Resistor Mini [tolerance=±5% resistance=470 package=THT]
  R3 = Resistor Mini [tolerance=±5% resistance=470 package=THT]
  R4 = Resistor Mini [tolerance=±5% resistance=470 package=THT]
  R5 = Resistor Mini [tolerance=±5% resistance=470 package=THT]
  R6 = Resistor Mini [tolerance=±5% resistance=470 package=THT]
  R7 = Resistor Mini [tolerance=±5% resistance=470 package=THT]
  R8 = Resistor Mini [tolerance=±5% resistance=470 package=THT]
  R9 = Resistor Mini [tolerance=±5% resistance=470 package=THT]
  R10 = Resistor Mini [tolerance=±5% resistance=470 package=THT]
  R11 = Resistor Mini [tolerance=±5% resistance=470 package=THT]
  R12 = Resistor Mini [tolerance=±5% resistance=470 package=THT]
  R13 = Resistor Mini [tolerance=±5% resistance=470 package=THT]
  R14 = Resistor Mini [tolerance=±5% resistance=470 package=THT]
  R15 = Resistor Mini [tolerance=±5% resistance=470 package=THT]
  R16 = Resistor Mini [tolerance=±5% resistance=470 package=THT]
  BLBUTLED = LED - 5mm [color="Red (633nm)" package="5 mm [THT]"]
  YELSWLED = LED - 5mm [color="Blue (525nm)" package="5 mm [THT]"]
  REDBTNLED = LED - 5mm [color="Green (570nm)" package="5 mm [THT]"]
  WHSWLED = LED - 5mm [color="Yellow (595nm)" package="5 mm [THT]"]
  GRBUTLED = LED - 5mm [color="Red (633nm)" package="5 mm [THT]"]
  REDSWLED = LED - 5mm [color="Blue (525nm)" package="5 mm [THT]"]
  YELBTNLED = LED - 5mm [color="Green (570nm)" package="5 mm [THT]"]
  R17 = Resistor Mini [tolerance=±5% resistance=470 package=THT]
  DFRobot_DFPlayer_Mini1 = DFRobot DFPlayer Mini [part_number=DFR0299]
  SP1 = SPEAKER [package=pcb_mount_speaker]
  BLUEBTN = Waterproof Pushbutton (blue)
  REDBTN = Waterproof Pushbutton (red)
  YELBTN = Waterproof Pushbutton (white)
  GRNBTN = Waterproof Pushbutton (green)
  R19 = Resistor Mini [tolerance=±5% resistance=470 package=THT]
  R20 = Resistor Mini [tolerance=±5% resistance=470 package=THT]
  YELLSW = Toggle Switch [package=THT]
  WHSW = Toggle Switch [package=THT]
  REDSW = Toggle Switch [package=THT]
  R21 = Resistor Mini [tolerance=±5% resistance=10k package=THT]
  R22 = Resistor Mini [tolerance=±5% resistance=10k package=THT]
  R23 = Resistor Mini [tolerance=±5% resistance=10k package=THT]
  J1 = Infrared Proximity Sensor
  Voltmeter1 = Voltmeter
  FANPOT = SLIDER [package=slider]
  F1 = Fan - Ventilador [package=THT]
  Part2 = Adafruit TB6612 DC and Stepper Motor Driver [part_number="Adafruit #2448"]
  MOTORPOWER = RioRand LM2596
  NEOPIXELPOWER = RioRand LM2596
  Power_plug1 = Power plug
  J2 = Basic Force Sensing Resistor (FSR) [package=THT]
  U1 = Vibration Motor- ROB-08449 [package=vibe-motor-10mm]
  R24 = Resistor Mini [tolerance=±5% resistance=10k package=THT]  # not connected
  R25 = Resistor Mini [tolerance=±5% resistance=10k package=THT]
  Part3 = MPR121 Breakout
  PHONE = Photocell (LDR) [package=THT]
  R26 = Resistor Mini [tolerance=±5% resistance=10k package=THT]
  R27 = Resistor Mini [tolerance=±5% resistance=470 package=THT]
  REDPOT = Rotary Potentiometer (Large) [maximum_resistance=100kΩ package=THT]
  GREENPOT = Rotary Potentiometer (Large) [maximum_resistance=100kΩ package=THT]
  BLUEPOT = Rotary Potentiometer (Large) [maximum_resistance=100kΩ package=THT]
  LED1 = RGB LED (com. cathode, rgb) [package="5 mm [THT]"]
  R28 = Resistor Mini [tolerance=±5% resistance=470 package=THT]
  R29 = Resistor Mini [tolerance=±5% resistance=470 package=THT]
  R30 = Resistor Mini [tolerance=±5% resistance=470 package=THT]
  U2 = WS2812 RGB LED strip
  ENCODER1 = Rotary Encoder with Knob
  R31 = Resistor Mini [tolerance=±5% resistance=1k package=THT]

nets:
  N1: Part1.A8, J2.pin_0, R25.Pin_1
  N2: Part1.A0, REDPOT.wiper
  N3: Part1.A1, GREENPOT.wiper
  N4: Part1.A2, BLUEPOT.wiper
  N5: Part1.A3, J1.Vout
  N6: Part1.A4, ENCODER1.no_name_yet#3
  N7: Part1.A5, ENCODER1.no_name_yet#1
  N8: Part1.A6, ENCODER1.no_name_yet#4
  N9: Part1.A7, FANPOT.A
  N10: Part1.D21/SCL, Part3.SCL
  N11: Part1.D20/SDA, Part3.SDA
  N12: Part1.D11_PWM, R31.Pin_0
  N13: Part1.D10_PWM, DFRobot_DFPlayer_Mini1.TX
  N14: Part1.D9_PWM, LED1.blue_anode, R30.Pin_0, R30.Pin_1
  N15: Part1.D8_PWM, LED1.green_anode, R29.Pin_0, R29.Pin_1
  VCC: Part1.5V, SR1.MR, SR1.VCC, SR2.MR, SR2.VCC, C1.1, C1_2.1, C1_3.1, C2.1, DFRobot_DFPlayer_Mini1.VCC, BLUEBTN.no_name_yet#4, REDBTN.no_name_yet#4, YELBTN.no_name_yet#4, GRNBTN.no_name_yet#4, R19.Pin_0, R19.Pin_1, R20.Pin_0, R20.Pin_1, YELLSW.COM, WHSW.COM, REDSW.COM, J1.Vcc, FANPOT.S, Part2.VCC, J2.pin_1, Part3.3.3V, R26.Pin_0, REDPOT.leg2, GREENPOT.leg2, BLUEPOT.leg2
  GND: Part1.GND, SR1.GND, SR1.OE, SR2.GND, SR2.OE, C1.0, C1_2.0, C1_3.0, PHLED0.cathode, C2.0, PHLED1.cathode, PHLED2.cathode, PHLED3.cathode, PHLED4.cathode, PHLED5.cathode, PHLED6.cathode, PHLED7.cathode, PHLED8.cathode, PHLED9.cathode, BLBUTLED.cathode, YELSWLED.cathode, REDBTNLED.cathode, WHSWLED.cathode, GRBUTLED.cathode, REDSWLED.cathode, YELBTNLED.cathode, DFRobot_DFPlayer_Mini1.GND-1, DFRobot_DFPlayer_Mini1.GND-2, BLUEBTN.no_name_yet#1, BLUEBTN.no_name_yet#5, REDBTN.no_name_yet#1, REDBTN.no_name_yet#5, YELBTN.no_name_yet#1, YELBTN.no_name_yet#5, GRNBTN.no_name_yet#1, GRNBTN.no_name_yet#5, YELLSW.L2, WHSW.L2, REDSW.L2, R21.Pin_1, R22.Pin_0, R23.Pin_1, J1.GND, Voltmeter1.Com, FANPOT.E, Part2.GND, MOTORPOWER.Pin_4, NEOPIXELPOWER.Pin_4, R25.Pin_0, Part3.GND, PHONE.pin_0, REDPOT.leg1, GREENPOT.leg1, BLUEPOT.leg1, LED1.common_cathode, U2.GND, ENCODER1.no_name_yet#2, ENCODER1.no_name_yet#5
  N16: Part1.D2_PWM, Part2.PWMA
  N17: Part1.D3_PWM, Part2.PWMB
  N18: Part1.D4_PWM, Voltmeter1.Positive
  N19: Part1.D6_PWM, U2.DIN
  N20: Part1.D7_PWM, LED1.red_anode, R28.Pin_0, R28.Pin_1
  N21: Part1.D22, SR1.DS
  N22: Part1.D23, SR1.SH_CP, SR2.SH_CP
  N23: Part1.D24, SR1.ST_CP, SR2.ST_CP
  N24: Part1.D25, YELBTNLED.anode, R17.Pin_0, R17.Pin_1
  N25: Part1.D26, REDBTN.no_name_yet#3
  N26: Part1.D27, YELLSW.L1, R21.Pin_0
  N27: Part1.D28, BLUEBTN.no_name_yet#3
  N28: Part1.D29, WHSW.L1, R22.Pin_1
  N29: Part1.D30, GRNBTN.no_name_yet#3
  N30: Part1.D31, REDSW.L1, R23.Pin_0
  N31: Part1.D32, YELBTN.no_name_yet#3
  N32: Part1.D33, PHONE.pin_1, R26.Pin_1, R27.Pin_0, R27.Pin_1
  N33: Part1.D42, Part2.BIN2
  N34: Part1.D43, Part2.BIN1
  N35: Part1.D44, Part2.AIN2
  N36: Part1.D45, Part2.AIN1
  N37: Part1.D52, Part2.STBY
  N38: SR1.Q1, PHLED1.anode, R2.Pin_0, R2.Pin_1
  N39: SR1.Q2, PHLED2.anode, R3.Pin_0, R3.Pin_1
  N40: SR1.Q3, PHLED3.anode, R4.Pin_0, R4.Pin_1
  N41: SR1.Q4, PHLED4.anode, R5.Pin_0, R5.Pin_1
  N42: SR1.Q5, PHLED5.anode, R6.Pin_0, R6.Pin_1
  N43: SR1.Q6, PHLED6.anode, R7.Pin_0, R7.Pin_1
  N44: SR1.Q7, PHLED7.anode, R8.Pin_0, R8.Pin_1
  N45: SR1.Q7', SR2.DS
  N46: SR1.Q0, PHLED0.anode, R1.Pin_0, R1.Pin_1
  N47: SR2.Q1, PHLED9.anode, R10.Pin_0, R10.Pin_1
  N48: SR2.Q2, R11.Pin_0, R11.Pin_1, REDBTNLED.anode
  N49: SR2.Q3, R12.Pin_0, R12.Pin_1, YELSWLED.anode
  N50: SR2.Q4, R13.Pin_0, R13.Pin_1, BLBUTLED.anode
  N51: SR2.Q5, R14.Pin_0, R14.Pin_1, WHSWLED.anode
  N52: SR2.Q6, R15.Pin_0, R15.Pin_1, GRBUTLED.anode
  N53: SR2.Q7, R16.Pin_0, R16.Pin_1, REDSWLED.anode
  N54: SR2.Q0, PHLED8.anode, R9.Pin_0, R9.Pin_1
  N55: DFRobot_DFPlayer_Mini1.RX, R31.Pin_1
  N56: DFRobot_DFPlayer_Mini1.SPK_1, SP1.-
  N57: DFRobot_DFPlayer_Mini1.SPK_2, SP1.+
  N58: F1.5V, Part2.MOTORA1
  N59: F1.GND, Part2.MOTORA2
  N60: Part2.PWRIN, MOTORPOWER.Pin_3
  N61: Part2.MOTORB2, U1.+
  N62: Part2.MOTORB1, U1.-
  N63: MOTORPOWER.Pin_1, NEOPIXELPOWER.Pin_1, Power_plug1.VCC
  N64: MOTORPOWER.Pin_2, NEOPIXELPOWER.Pin_2, Power_plug1.GND
  N65: NEOPIXELPOWER.Pin_3, U2.VCC

notes:
  Duck
  Phone
  I did not use this diagram, and don't recommend you use it!

custom parts:
  Resistor Mini: A generic resistor (0.25W)
  Waterproof Pushbutton (blue): Waterproof Illuminated Pushbutton (blue)
  Waterproof Pushbutton (red): Waterproof Illuminated Pushbutton (red)
  Waterproof Pushbutton (white): Waterproof Illuminated Pushbutton (white)
  Waterproof Pushbutton (green): Waterproof Illuminated Pushbutton (green)
  Voltmeter: A Standard Multimeter in Current mode
  Fan - Ventilador: Ventilador de 2 pines, se encuentra comunmente en computadoras de escritorio
  Adafruit TB6612 DC and Stepper Motor Driver: Spin two DC motors, step one bi-polar or uni-polar stepper, or fire off two solenoids with 1.2A per channel using the TB6612. These are perhaps better known as "the drivers in our assembled Adafruit Motorshield or Motor HAT." We really like these dual H-bridges, so if you want to control motors without a shield or HAT these are easy to include on any solderless breadboard or perma-proto.
  WS2812 RGB LED strip: WS2812 strip
  Rotary Encoder with Knob: Rotary Encoder with 1/4" Shaft and Knob
